// Logisim project Etapa1.circ as structural Verilog: 1 circuit, main circuit main
module main (
  input  A,
  input  B,
  input  C,
  input  D,
  input  E,
  output [8:0] SALIDA
);

  wire clock_1_out, undriven, undriven_2;
  wire [2:0] rom_1_data;

  ROM #(.addrWidth(3), .dataWidth(3)) rom_1 (.data(rom_1_data));  // open: addr
  Multiplexer #(.select(3)) multiplexer_1 ();  // open: in0, in1, in2, in3, in4, in5, in6, in7, out, sel
  Clock clock_1 (.out(clock_1_out));
  Counter #(.max('h7), .width(3)) counter_1 (
    .clr(undriven_2), .load(undriven), .up(1'b1), .count(1'b1), .clk(clock_1_out), .D(rom_1_data),
    .Q(SALIDA[2:0]));  // open: carry
  not not_1 (SALIDA[8], 1'b0);

  assign SALIDA[7:3] = {5{1'b0}};

  // Notes on the sheet:
  //   ENTRADAS
endmodule
